# Fritzing sketch LCR_meter (saved by Fritzing 0.9.3b)
breadboards: 1

parts:
  R1 = Resistor [tolerance=±5% resistance=220 package=THT]
  R2 = Resistor [tolerance=±5% resistance=10k package=THT]
  Grove1 = Grove OLED 128x96
  Part1 = Arduino Uno (Rev3) - ICSP
  S1 = Pushbutton [package="[THT]"]
  S2 = Pushbutton [package="[THT]"]
  J2 = Screw terminal - 2 pins [package=THT]  # not connected
  J3 = Screw terminal - 2 pins [package=THT]
  J1 = screw terminal, 2 pins
  J1_2 = Screw terminal - 2 pins [package=THT]

nets:
  N1: R1.Pin_0, R2.Pin_1, Part1.A0, J1.pin2, J1_2.pin2
  N2: R1.Pin_1, Part1.D11_PWM/MOSI
  N3: R2.Pin_0, Part1.D12/MISO
  GND: Grove1.GND, Part1.D2, Part1.D3_PWM, Part1.GND, S1.Pin_3, S1.Pin_4, S2.Pin_3, S2.Pin_4, J1.pin1, J1_2.pin1
  VCC: Grove1.VCC, Part1.5V
  N4: Grove1.SDA, Part1.A4/SDA
  N5: Grove1.SCL, Part1.A5/SCL
  N6: Part1.A2, J3.pin1
  N7: Part1.A3, J3.pin2
  N8: S1.Pin_1, S1.Pin_2
  N9: S2.Pin_1, S2.Pin_2

notes:
  test1
  terminal
  test2
  terminal
