# Fritzing sketch LCR_meter (saved by Fritzing 0.9.3b)
breadboards: 1

parts:
  R1 = Resistor [tolerance=±5% resistance=220 package=THT]
  R2 = Resistor [tolerance=±5% resistance=10k package=THT]
  Grove1 = Grove OLED 128x96
  S1 = Pushbutton [package="[THT]"]
  S2 = Pushbutton [package="[THT]"]
  J3 = Screw terminal - 2 pins [package=THT]
  J1 = screw terminal, 2 pins
  J1_2 = Screw terminal - 2 pins [package=THT]
  Part2 = Arduino Nano (Rev3.0) (ICSP)
  S3 = Pushbutton [package="[THT]"]
  J4 = Screw terminal - 2 pins [package=THT]
  R3 = Resistor [tolerance=±5% resistance=3.1k package=THT]
  R4 = Resistor [tolerance=±5% resistance=1.8k package=THT]
  R5 = Resistor [tolerance=±5% resistance=10k package=THT]

nets:
  N1: R1.Pin_0, R2.Pin_1, J1.pin2, J1_2.pin2, Part2.A7
  N2: R1.Pin_1, Part2.D11/MOSI
  N3: R2.Pin_0, Part2.D12/MISO
  GND: Grove1.GND, S1.Pin_3, S1.Pin_4, S2.Pin_3, S2.Pin_4, J1.pin1, J1_2.pin1, Part2.D3, Part2.D5, Part2.D8, Part2.GND, S3.Pin_3, S3.Pin_4, J4.pin1, R3.Pin_0
  VCC: Grove1.VCC, Part2.5V, R4.Pin_0
  N4: Grove1.SDA, Part2.A4
  N5: Grove1.SCL, Part2.A5
  N6: S1.Pin_1, S1.Pin_2
  N7: S2.Pin_1, S2.Pin_2
  N8: J3.pin1, Part2.A2
  N9: J3.pin2, Part2.A3
  N10: Part2.D2, R5.Pin_1
  N11: Part2.D6, J4.pin2, R5.Pin_0
  N12: Part2.D7, R3.Pin_1, R4.Pin_1
  N13: S3.Pin_1, S3.Pin_2

notes:
  test1
  terminal
  test2
  terminal
  [test 3 terminal]
